# Fritzing sketch Power monitor (saved by Fritzing 1.0.8)

parts:
  Part1 = INA219 High Side DC Current Sensor Breakout [part_number=904]
  U2 = XIAO ESP32C3
  R2 = Resistor [tolerance=±5% resistance=4.7k package="1206 [SMD]"]  # not connected
  DS1 = DS18B20 1-Wire Temperature Sensor [part_number=DS18B20]

nets:
  VCC: Part1.VCC, U2.3V3, DS1.VDD
  N1: Part1.SCL, U2.D5
  N2: Part1.SDA, U2.D4
  N3: U2.D6, DS1.DQ
  GND: U2.GND, DS1.GND

notes:
  5v
  6-16v
  4k7

custom parts:
  INA219 High Side DC Current Sensor Breakout: This breakout board will solve all your power-monitoring problems. Instead of struggling with two multimeters, you can just use the handy INA219B chip on this breakout to both measure both the high side voltage and DC current draw over I2C with 1% precision. Most current-measuring devices such as our current panel meter are only good for low side measuring. That means that unless you want to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
  XIAO ESP32C3: Seeed Studio XIAO ESP32C3 adopts new RISC-V architecture, supporting both Wi-Fi and BLE wireless connectivities. For Internet of Things applications, you will find it is flexible and suitable for all kinds of IoT scenarios.
