# Fritzing sketch RipTide (saved by Fritzing 1.0.4)
stripboards: 1

parts:
  A1 = Littlebee 40A ESC  # not connected
  A2 = DYS BE1806  # not connected
  DS1 = DS18B20 1-Wire Temperature Sensor [part_number=DS18B20]  # not connected
  Part13 = InvenSense MPU6050  # not connected
  A3 = 2957N11 pressure sensor  # not connected
  Part14 = 24 NeoPixel Ring [part_number=1586]  # not connected
  J10 = screw terminal, 2 pins  # not connected
  Part9 = TFT 2.8 inch 320x240 Touch w microSD [part_number=1770]  # not connected
  J15 = Generic male header - 1 pins [form="♂ (male)" package=THT]  # not connected
  J17 = Generic male header - 1 pins [form="♂ (male)" package=THT]  # not connected
  J18 = Generic male header - 1 pins [form="♂ (male)" package=THT]  # not connected
  J21 = Generic male header - 1 pins [form="♂ (male)" package=THT]  # not connected
  J23 = Generic male header - 1 pins [form="♂ (male)" package=THT]
  F2 = Resettable Fuse PTC [package=ptc]  # not connected
  C2 = Electrolytic Capacitor [capacitance=10μF voltage=35V package="100 mil [THT, electrolytic]"]  # not connected
  J24 = Generic male header - 1 pins [form="♂ (male)" package=THT]  # not connected
  J25 = Generic male header - 1 pins [form="♂ (male)" package=THT]  # not connected
  Part20 = Adafruit Breadboard-Friendly NeoPixel [part_number="Adafruit #1312"]  # not connected
  S4 = Hall Sensor [part_number=WSH130 package=TO92]  # not connected
  microSD_Transflash1 = SparkFun - microSD Transflash  # not connected
  S6 = Reed switch [package=THT]  # not connected
  J27 = Generic male header - 1 pins [form="♂ (male)" package=THT]  # not connected
  J3 = rounded female pin header, 12 pins [form="♀ (female rounded)"]  # not connected
  R2 = Resistor [tolerance=±5% power=0.25W resistance=10k package=THT]  # not connected
  C5 = Ceramic Capacitor [capacitance=100nF voltage=35V package="100 mil [THT, multilayer]"]  # not connected
  J29 = Generic male header - 1 pins [form="♂ (male)" package=THT]  # not connected
  J31 = Generic male header - 1 pins [form="♂ (male)" package=THT]  # not connected
  C6 = Ceramic Capacitor [capacitance=100nF voltage=35V package="100 mil [THT, multilayer]"]
  J32 = Generic male header - 1 pins [form="♂ (male)" package=THT]  # not connected
  J33 = Generic male header - 1 pins [form="♂ (male)" package=THT]  # not connected
  J35 = Generic male header - 1 pins [form="♂ (male)" package=THT]  # not connected
  J36 = rounded female pin header, 4 pins [form="♀ (female rounded)"]  # not connected
  J37 = Generic male header - 1 pins [form="♂ (male)" package=THT]  # not connected
  J40 = Generic male header - 1 pins [form="♂ (male)" package=THT]  # not connected
  M1 = xy-mos d4184 [package=THT]
  J41 = Generic male header - 1 pins [form="♂ (male)" package=THT]
  J42 = Generic male header - 1 pins [form="♂ (male)" package=THT]
  J43 = Generic male header - 1 pins [form="♂ (male)" package=THT]  # not connected
  M2 = xy-mos d4184 [package=THT]
  J46 = Generic male header - 1 pins [form="♂ (male)" package=THT]  # not connected
  J26 = rounded female pin header, 4 pins [form="♀ (female rounded)"]  # not connected
  J48 = screw terminal, 2 pins  # not connected
  J50 = screw terminal, 2 pins  # not connected
  J51 = Generic male header - 1 pins [form="♂ (male)" package=THT]  # not connected
  J53 = Generic male header - 1 pins [form="♂ (male)" package=THT]  # not connected
  J52 = rounded female pin header, 3 pins [form="♀ (female rounded)"]  # not connected
  J54 = screw terminal, 2 pins  # not connected
  J8 = rounded female pin header, 12 pins [form="♀ (female rounded)"]  # not connected
  J44 = rounded female pin header, 12 pins [form="♀ (female rounded)"]  # not connected
  J47 = single row smd female pin header, 1 pin [form="♀ (female)"]  # not connected
  J55 = Generic male header - 1 pins [form="♂ (male)" package=THT]  # not connected
  F3 = Resettable Fuse PTC [package=ptc]  # not connected
  F4 = Resettable Fuse PTC [package=ptc]  # not connected
  J56 = Generic male header - 1 pins [form="♂ (male)" package=THT]  # not connected
  J57 = Generic male header - 1 pins [form="♂ (male)" package=THT]  # not connected
  J58 = Generic male header - 1 pins [form="♂ (male)" package=THT]  # not connected
  J59 = Generic male header - 1 pins [form="♂ (male)" package=THT]  # not connected

nets:
  N1: J23.Ground, C6.1
  N2: M1.pin1, M1.pin3, M1.pin4
  N3: M1.pin2, M1.pin5, M1.pin6, M1.pin7, J42.Ground
  N4: J41.Ground, M2.pin2, M2.pin5, M2.pin6, M2.pin7
  N5: M2.pin1, M2.pin3, M2.pin4

notes:
  Display
  Reset
  SPI Clock
  I2C
  Data cmd
  MISO
  MOSI
  Chip select
  Led backlight
  SD Card
  Throttle/btns
  Gyro
  Pressure
  Throttleds
  5v
  3.3v
  Pixels
  ESC
  One wire
  Extra
  Buzzer
  BMS
  N/C
  Fuse

custom parts:
  Littlebee 40A ESC: LittleBee 40A 2-4 LiPo Battery ESC Brushless Speed Controller for RC FPV Multicopter.
  DYS BE1806: quadcopter brushless motor.
  2957N11 pressure sensor: Monitor and control vacuum pumps, air compressors, and hydraulics. These transmitters convert both pressure and vacuum into an electrical signal that can be interpreted by receiving devices, such as remote displays, programmable logic controllers, and motor speed controls.
  24 NeoPixel Ring: 24 ultra bright smart LED NeoPixels are arranged in a circle with 2.6" (66mm) outer diameter. The rings are 'chainable' - connect the output pin of one to the input pin of another. Use only one microcontroller pin to control as many as you can chain together! Each LED is addressable as the driver chip is inside the LED. Each one has ~18mA constant current drive so the color will be very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
  TFT 2.8 inch 320x240 Touch w microSD: This TFT display is big (2.8" diagonal) bright (4 white-LED backlight) and colorful! 240x320 pixels with individual RGB pixel control. As a bonus, this display has a resistive touchscreen attached to it already, so you can detect finger presses anywhere on the screen.
  Generic male header - 1 pins: Generic male header
  Adafruit Breadboard-Friendly NeoPixel: This is the easiest way possible to add small, bright RGB pixels to your project. We took the same technology from our Flora NeoPixels and made them breadboard friendly, with two rows of 3 x 0.1" spaced header on each side for easy soldering, chaining and breadboarding. These ultra-bright LEDs have a constant-current driver cooked right into the LED package! The pixels are chainable - so you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
  Hall Sensor: A Hall Sensor
  xy-mos d4184: xy-mos d4184 Two parallel N-Channel logic compatible MOSFETS with low Rds(on) for high current low-side switching applications.
