# Fritzing sketch xiao-esp32c3-schematic (saved by Fritzing 1.0.4)

parts:
  U2 = XIAO ESP32C3
  5K = Resistor [tolerance=±5% power=0.5W resistance=6.8k package=THT]  # not connected
  J1 = Dagu DGServo 9g header (male) [package=THT]
  J2 = Dagu DGServo 9g header (male) [package=THT]
  M1 = BME680 Module [part_number=CJMCU-680]

nets:
  N1: U2.D4, M1.SDA
  N2: U2.D5, M1.SCL
  N3: U2.D7, J1.Vcc
  3V3: U2.3V3, J2.Vcc
  GND: U2.GND, J2.gnd
  N4: U2.5V, J2.pulse

notes:
  GPIO20
  GND
  5V
  3V3
  Data GND
  1
  6
  RJ12
  GPIO6
  GPIO7
  BME680

custom parts:
  XIAO ESP32C3: Seeed Studio XIAO ESP32C3 adopts new RISC-V architecture, supporting both Wi-Fi and BLE wireless connectivities. For Internet of Things applications, you will find it is flexible and suitable for all kinds of IoT scenarios.
  BME680 Module: Bosch BME680 Development Module The BME680 is a digital 4-in-1 sensor that measures air quality [gas], humidity, pressure and temperature. Links: BME680 product datasheet
